# Fritzing sketch Arduino (saved by Fritzing 0.9.4)
breadboards: 1

parts:
  J1 = Generic female header - 10 pins [form="♀ (female)" package=THT]
  BT1 = Bluetooth HC-06u [package=THT]
  LED1 = LED - 5mm [color="Yellow (595nm)" package="5 mm [THT]"]
  R1 = Resistor [tolerance=±5% resistance=200 package=THT]
  부품1 = Arduino Uno (Rev3)
  J2 = Generic female header - 10 pins [form="♀ (female)" package=THT]
  J3 = Generic female header - 10 pins [form="♀ (female)" package=THT]

nets (from the breadboard view):
  VCC: J1.VCC, J1.POWER_VCC, BT1.VCC, 부품1.5V, J2.VCC, J2.POWER_VCC, J3.VCC, J3.POWER_VCC
  GND: J1.GND, J1.POWER_GND, BT1.GND, R1.Pin_1, 부품1.GND, J2.GND, J2.POWER_GND, J3.GND, J3.POWER_GND
  N1: J1.DATA, 부품1.D4
  N2: J1.LATCH, 부품1.D5_PWM
  N3: J1.CLOCK, 부품1.D6_PWM
  N4: BT1.TXD, 부품1.D3_PWM
  N5: BT1.RXD, 부품1.D2
  N6: LED1.cathode, R1.Pin_0
  N7: LED1.anode, 부품1.D13/SCK
  N8: 부품1.D8, J2.LATCH
  N9: 부품1.D9_PWM, J2.CLOCK
  N10: 부품1.D10_PWM/SS, J3.DATA
  N11: 부품1.D11_PWM/MOSI, J3.LATCH
  N12: 부품1.D12/MISO, J3.CLOCK
  N13: 부품1.D7, J2.DATA

notes:
  외부전력 SMPS로 공급

custom parts:
  Generic female header - 10 pins: Generic female header
  Bluetooth HC-06u: Bluetooth HC-06 - face up, pins down 16.5mm x 37.5mm PCB
